# Fritzing sketch TestBoardWiring (saved by Fritzing 0.7.7b)
breadboards: 1

parts:
  LED1 = LED - 5mm [color="Red (633nm)" package="5 mm [THT]"]  # not connected
  Arduino1 = Arduino  # not connected
  S1 = Pushbutton [package="[THT]"]

nets:
  N1: S1.Pin_1, S1.Pin_2
  N2: S1.Pin_3, S1.Pin_4
